# Fritzing sketch EsquemaCI-AMega2560 (saved by Fritzing 0.9.3b)
circuit board: 30.5885cm x 19.2029cm

parts:
  YwRobot_Power_Supply = YwRobot Breadboard Power Supply [part_number=545043]
  Arduino_Mega_2560 = Arduino Mega 2560 (Rev3)
  Ethernet_Shield = Arduino Ethernet Shield (Rev3)
  Motor_Stepper = 28BYJ-48 Stepper Motor
  RFID = RFID-RC522-v3
  Display = LCD Keypad Shield
  Driver_Motor_Stepper = ULN2003A

nets:
  N1: YwRobot_Power_Supply.VCC#5, Display.+5V
  N2: YwRobot_Power_Supply.VCC#9, RFID.3.3V
  N3: YwRobot_Power_Supply.GND#11, Display.GND
  N4: YwRobot_Power_Supply.GND#13, RFID.GND
  N5: Arduino_Mega_2560.D22, Display.D4
  N6: Arduino_Mega_2560.D23, Display.D5
  N7: Arduino_Mega_2560.D24, Display.D6
  N8: Arduino_Mega_2560.D25, Display.D7
  N9: Arduino_Mega_2560.D26, Display.rs
  N10: Arduino_Mega_2560.D27, Display.en
  N11: Arduino_Mega_2560.D37, Driver_Motor_Stepper.1N4
  N12: Arduino_Mega_2560.D38, Driver_Motor_Stepper.1N3
  N13: Arduino_Mega_2560.D39, Driver_Motor_Stepper.1N2
  N14: Arduino_Mega_2560.D40, Driver_Motor_Stepper.1N1
  N15: Arduino_Mega_2560.D48, RFID.SDA
  N16: Arduino_Mega_2560.D49, RFID.RST
  N17: Arduino_Mega_2560.D50, RFID.MISO
  N18: Arduino_Mega_2560.D51, RFID.MOSI
  N19: Arduino_Mega_2560.D52, RFID.SCK
  N20: Ethernet_Shield.RESET, Display.RESET
  5V: Ethernet_Shield.5V, Driver_Motor_Stepper.+5V
  GND: Ethernet_Shield.GND, Driver_Motor_Stepper.GND
  VIN: Ethernet_Shield.VIN, Display.VIN
  N21: Motor_Stepper.RED, Driver_Motor_Stepper.YELLOW_wire
  N22: Motor_Stepper.ORANGE, Driver_Motor_Stepper.ORANGE_wire
  N23: Motor_Stepper.YELLOW, Driver_Motor_Stepper.RED_wire
  N24: Motor_Stepper.PINK, Driver_Motor_Stepper.PINK_wire
  N25: Motor_Stepper.BLUE, Driver_Motor_Stepper.BLUE_wire

custom parts:
  YwRobot Breadboard Power Supply: The YwRobot Breadboard Power Supply (MB-V2) has two power rails; they can be 5V or 3V3. Power to the module can be provided through the female USB socket or through the A10 (female) 2.1mm power jack.
  RFID-RC522-v3: A simple China made RFID-RC522 Reader (6x4 cm); do check the pin labels, as this is a MFRC522 based clone.
  LCD Keypad Shield: It consists of a 1602 white character blue backlight LCD. The keypad consists of 5 keys — select, up, right, down and left. To save the digital IO pins, the keypad interface uses only one ADC channel. The key value is read through a 5 stage voltage divider.
  ULN2003A: ULN2003A 7-way Darlington Transistor Driver on breakoutboard
