# Fritzing sketch EsquemaProtoboard (saved by Fritzing 0.9.3b)
breadboards: 1

parts:
  RFID = RFID-RC522-v3
  Arduino_UNO = Arduino Uno (Rev3)
  Display = DeuLigne 1.1 - The Snootlab's LCD shield for Arduino

nets:
  N1: RFID.SDA, Arduino_UNO.D10_PWM/SS, Display.D5
  N2: RFID.SCK, Arduino_UNO.D13/SCK, Display.D2
  N3: RFID.MOSI, Arduino_UNO.D11_PWM/MOSI, Display.D4
  N4: RFID.MISO, Arduino_UNO.D12/MISO, Display.D3
  GND: RFID.GND, Arduino_UNO.GND, Arduino_UNO.D1/TX, Display.GND, Display.D1_TX
  N5: RFID.RST, Arduino_UNO.D3_PWM, Display.D12_MISO
  3.3V: RFID.3.3V, Arduino_UNO.3V3
  N6: Arduino_UNO.A0, Display.A0
  N7: Arduino_UNO.A1, Display.A1
  N8: Arduino_UNO.A2, Display.A2
  N9: Arduino_UNO.A3, Display.A3
  N10: Arduino_UNO.A4/SDA, Display.A4(SDA)
  N11: Arduino_UNO.A5/SCL, Display.A5(CLK)
  N12: Arduino_UNO.D8, Display.D7
  N13: Arduino_UNO.D9_PWM, Display.D6
  N14: Arduino_UNO.AREF, Display.D0_RX
  N15: Arduino_UNO.D0/RX, Display.AREF
  N16: Arduino_UNO.D2, Display.D13_SCK
  N17: Arduino_UNO.D4, Display.D11_MOSI
  N18: Arduino_UNO.D5_PWM, Display.D10_SS
  N19: Arduino_UNO.D6_PWM, Display.D9
  N20: Arduino_UNO.D7, Display.D8
  N21: Arduino_UNO.RESET, Display.RESET
  5V: Arduino_UNO.5V, Display.+5V
  VIN: Arduino_UNO.VIN, Display.VIN

custom parts:
  RFID-RC522-v3: A simple China made RFID-RC522 Reader (6x4 cm); do check the pin labels, as this is a MFRC522 based clone.
